# Fritzing sketch arduilamp (saved by Fritzing 0.9.4)
circuit board: 4.40313cm x 1.88273cm
breadboards: 1

parts:
  R2 = Resistor [tolerance=±5% resistance=220 package=THT]
  R3 = Resistor [tolerance=±5% resistance=220 package=THT]
  R4 = Resistor [tolerance=±5% resistance=220 package=THT]
  Part1 = Arduino Nano (Rev3.0)

nets:
  N1: R2.Pin_0, Part1.D10
  N2: R2.Pin_1, R3.Pin_1, R4.Pin_1, Part1.GND
  N3: R3.Pin_0, Part1.D11/MOSI
  N4: R4.Pin_0, Part1.D12/MISO

notes:
  B1-
  B2-
  B3-
  B3+
  B2+
  B1+
  5V
  DIN
  GND
  1.1.0
